# Fritzing sketch schematic (saved by Fritzing 0.9.3b)
breadboards: 1

parts:
  Q1 = NPN-Transistor [package="TO92 [THT]"]
  R1 = Resistor [tolerance=±5% resistance=220 package=THT]
  D1 = Rectifier Diode [part_number=1N4001 package="300 mil [THT]"]
  Part1 = Arduino Uno (Rev3)
  R2 = Resistor [tolerance=±5% resistance=10k package=THT]
  J1 = female pin header, 4 pins [form="♀ (female)"]
  J2 = female pin header, 2 pins [form="♀ (female)"]
  J3 = female pin header, 3 pins [form="♀ (female)"]
  S1 = Pushbutton [package="[THT]"]
  R3 = Resistor [tolerance=±5% resistance=10k package=THT]

nets:
  GND: Q1.E, D1.anode, Part1.GND, J1.pin4, J2.pin2, J3.pin3, S1.Pin_1, S1.Pin_2
  N1: Q1.B, R1.Pin_1
  N2: Q1.C, D1.cathode, J1.pin2
  N3: R1.Pin_0, Part1.D5_PWM
  N4: Part1.D8, J3.pin2
  N5: Part1.D2, S1.Pin_3, S1.Pin_4, R3.Pin_1
  N6: Part1.D6_PWM, R2.Pin_0, J1.pin1
  N7: Part1.D7, J3.pin1
  5V: Part1.5V, R2.Pin_1, R3.Pin_0
  13.8V: Part1.VIN, J1.pin3, J2.pin1

notes:
  13.8 V
  to ICOM tuner
  to Yaesu CAT
  Key
  Start
  Rx
  Tx
